# Fritzing sketch analog-read (saved by Fritzing 0.9.1b)
breadboards: 1

parts:
  POT1 = Breadboard Trimpot
  Part1 = Tessel 2

nets:
  N1: POT1.PIN1, Part1.3V3
  N2: POT1.PIN2, Part1.7
  N3: POT1.PIN3, Part1.GND

custom parts:
  Tessel 2: Draft version of Tessel 2
