# Fritzing sketch digital-write (saved by Fritzing 0.9.1b)
breadboards: 1

parts:
  LED1 = smd LED [color="Red (633nm)" package="0603 [SMD]"]
  Part1 = Tessel 2

nets:
  N1: LED1.cathode, Part1.GND
  N2: LED1.anode, Part1.0

custom parts:
  Tessel 2: Draft version of Tessel 2
