# Fritzing sketch i2c-blinkm-controller (saved by Fritzing 0.9.1b)

parts:
  Part1 = BlinkM
  Part2 = Tessel 2

nets:
  N1: Part1.SDA, Part2.1
  N2: Part1.SCL, Part2.0
  GND: Part1.GND, Part2.GND
  VCC: Part1.VCC, Part2.3V3

custom parts:
  BlinkM: BlinkM component
  Tessel 2: Draft version of Tessel 2
