# Fritzing sketch pwm-rgb-led (saved by Fritzing 0.9.3b)
breadboards: 1

parts:
  Part1 = Tessel 2
  Q1 = MOSFET-NCHANNEL [package=to220v]
  Q2 = MOSFET-NCHANNEL [package=to220v]
  Q3 = MOSFET-NCHANNEL [package=to220v]
  LED1 = Super Flux RGB LED (com. cathode)
  12v_pwr = Camdenboss CTB0158-2 [package=THT]

nets:
  N1: Part1.GND, 12v_pwr.terminal_1
  N2: Part1.5#35, Q2.G
  N3: Part1.6, Q3.G
  N4: Part1.5#75, Q1.G
  N5: Q1.D, LED1.blue_anode
  N6: Q1.S, Q2.S, Q3.S
  N7: Q2.D, LED1.red_anode
  N8: Q3.D, LED1.green_anode
  N9: LED1.common_cathode, 12v_pwr.terminal_2

custom parts:
  Tessel 2: Draft version of Tessel 2
