# Fritzing sketch sensor-controlled-led (saved by Fritzing 0.9.1b)
breadboards: 1

parts:
  LED1 = smd LED [color="Red (633nm)" package="0603 [SMD]"]
  POT1 = Breadboard Trimpot
  Part1 = Tessel 2

nets:
  N1: LED1.cathode, POT1.PIN3, Part1.GND
  N2: LED1.anode, Part1.7#77
  N3: POT1.PIN1, Part1.3V3
  N4: POT1.PIN2, Part1.7#37

custom parts:
  Tessel 2: Draft version of Tessel 2
